// Logisim project project-checkers.circ as structural Verilog: 3 circuits, main circuit main
module main (
);

  wire button_1_out, clock, comparator_1_lt, comparator_2_eq, comparator_3_eq, deshifrator, dev_read,
       dev_write, mem, not_1_out, not_2_out, read, word;
  wire [5:0] undriven;
  wire [15:0] address_bus, bit_extender_1_out, cdm16_1_p1, cdm16_1_p2, cdm16_1_p4, cdm16_1_p5, cdm16_1_p6,
       cdm16_1_p7, cdm16_1_p8, cdm16_1_p9, cdm16_1_p14, cdm16_1_p15, data_bus, register_1_q;
  wire [31:0] square_32_1_bus_0_2, square_32_1_bus_0_3, square_32_1_bus_0_4, square_32_1_bus_0_5,
       square_32_2_bus_0_2, square_32_2_bus_0_3, square_32_2_bus_0_4, square_32_2_bus_0_5,
       square_32_3_bus_0_2, square_32_3_bus_0_3, square_32_3_bus_0_4, square_32_3_bus_0_5,
       square_32_4_bus_0_2, square_32_4_bus_0_3, square_32_4_bus_0_4, square_32_4_bus_0_5,
       square_32_5_bus_0_2, square_32_5_bus_0_3, square_32_5_bus_0_4, square_32_5_bus_0_5,
       square_32_6_bus_0_2, square_32_6_bus_0_3, square_32_6_bus_0_4, square_32_6_bus_0_5,
       square_32_7_bus_0_2, square_32_7_bus_0_3, square_32_7_bus_0_4, square_32_7_bus_0_5,
       square_32_8_bus_0_2, square_32_8_bus_0_3, square_32_8_bus_0_4, square_32_8_bus_0_5;

  DotMatrix #(.matrixcols(8), .matrixrows(16)) dotmatrix_1 (
    .col0(cdm16_1_p1), .col1(cdm16_1_p2), .col2(cdm16_1_p4), .col3(cdm16_1_p5), .col4(cdm16_1_p6),
    .col5(cdm16_1_p7), .col6(cdm16_1_p8), .col7(cdm16_1_p9));
  // cdm16 cdm16_1: pin names not known; wires that end beside it: cdm16_1_p1, cdm16_1_p2, clock, cdm16_1_p4, cdm16_1_p5, cdm16_1_p6, cdm16_1_p7, cdm16_1_p8, cdm16_1_p9, mem, read, word, address_bus, cdm16_1_p14, cdm16_1_p15
  Clock clock_1 (.out(clock));
  // Probe on address_bus
  assign data_bus = not_1_out ? cdm16_1_p14 : 16'bz;  // Controlled_Buffer controlled_buffer_1
  not not_1 (not_1_out, read);
  assign cdm16_1_p15 = read ? data_bus : 16'bz;  // Controlled_Buffer controlled_buffer_2
  DotMatrix #(.matrixcols(32), .matrixrows(32)) dotmatrix_2 (
    .col0(32'hff00ff), .col1(32'hff00ff), .col2(32'hff00ff), .col3(32'hff00ff), .col4(32'hff00ff),
    .col5(32'hff00ff), .col6(32'hff00ff), .col7(32'hff00ff), .col8(32'hff00ff00), .col9(32'hff00ff00),
    .col10(32'hff00ff00), .col11(32'hff00ff00), .col12(32'hff00ff00), .col13(32'hff00ff00),
    .col14(32'hff00ff00), .col15(32'hff00ff00), .col16(32'hff00ff), .col17(32'hff00ff), .col18(32'hff00ff),
    .col19(32'hff00ff), .col20(32'hff00ff), .col21(32'hff00ff), .col22(32'hff00ff), .col23(32'hff00ff),
    .col24(32'hff00ff00), .col25(32'hff00ff00), .col26(32'hff00ff00), .col27(32'hff00ff00),
    .col28(32'hff00ff00), .col29(32'hff00ff00), .col30(32'hff00ff00), .col31(32'hff00ff00));
  DotMatrix #(.matrixcols(32), .matrixrows(32)) dotmatrix_3 (
    .col0(32'hff00ff), .col1(32'hff00ff), .col2(32'hff00ff), .col3(32'hff00ff), .col4(32'hff00ff),
    .col5(32'hff00ff), .col6(32'hff00ff), .col7(32'hff00ff), .col8(32'hff00ff00), .col9(32'hff00ff00),
    .col10(32'hff00ff00), .col11(32'hff00ff00), .col12(32'hff00ff00), .col13(32'hff00ff00),
    .col14(32'hff00ff00), .col15(32'hff00ff00), .col16(32'hff00ff), .col17(32'hff00ff), .col18(32'hff00ff),
    .col19(32'hff00ff), .col20(32'hff00ff), .col21(32'hff00ff), .col22(32'hff00ff), .col23(32'hff00ff),
    .col24(32'hff00ff00), .col25(32'hff00ff00), .col26(32'hff00ff00), .col27(32'hff00ff00),
    .col28(32'hff00ff00), .col29(32'hff00ff00), .col30(32'hff00ff00), .col31(32'hff00ff00));
  // Probe on data_bus
  // RAM ram_1: pin names not known; wires that end beside it: address_bus, word, deshifrator, clock, read, data_bus
  // Debugger debugger_1: pin names not known
  not not_2 (not_2_out, read);
  Comparator #(.width(16), .mode("unsigned")) comparator_1 (
    .a(address_bus), .b(16'h8000), .lt(comparator_1_lt));  // open: gt, eq
  Comparator #(.width(16), .mode("unsigned")) comparator_2 (
    .a(address_bus), .b(16'h8000), .eq(comparator_2_eq));  // open: gt, lt
  and and_1 (deshifrator, mem, comparator_1_lt);
  and and_2 (dev_write, mem, comparator_2_eq, not_2_out);
  DotMatrix #(.matrixcols(32), .matrixrows(32)) dotmatrix_4 (
    .col0(32'hff00ff), .col1(32'hff00ff), .col2(32'hff00ff), .col3(32'hff00ff), .col4(32'hff00ff),
    .col5(32'hff00ff), .col6(32'hff00ff), .col7(32'hff00ff), .col8(32'hff00ff00), .col9(32'hff00ff00),
    .col10(32'hff00ff00), .col11(32'hff00ff00), .col12(32'hff00ff00), .col13(32'hff00ff00),
    .col14(32'hff00ff00), .col15(32'hff00ff00), .col16(32'hff00ff), .col17(32'hff00ff), .col18(32'hff00ff),
    .col19(32'hff00ff), .col20(32'hff00ff), .col21(32'hff00ff), .col22(32'hff00ff), .col23(32'hff00ff),
    .col24(32'hff00ff00), .col25(32'hff00ff00), .col26(32'hff00ff00), .col27(32'hff00ff00),
    .col28(32'hff00ff00), .col29(32'hff00ff00), .col30(32'hff00ff00), .col31(32'hff00ff00));
  DotMatrix #(.matrixcols(32), .matrixrows(32)) dotmatrix_5 (
    .col0(32'hff00ff), .col1(32'hff00ff), .col2(32'hff00ff), .col3(32'hff00ff), .col4(32'hff00ff),
    .col5(32'hff00ff), .col6(32'hff00ff), .col7(32'hff00ff), .col8(32'hff00ff00), .col9(32'hff00ff00),
    .col10(32'hff00ff00), .col11(32'hff00ff00), .col12(32'hff00ff00), .col13(32'hff00ff00),
    .col14(32'hff00ff00), .col15(32'hff00ff00), .col16(32'hff00ff), .col17(32'hff00ff), .col18(32'hff00ff),
    .col19(32'hff00ff), .col20(32'hff00ff), .col21(32'hff00ff), .col22(32'hff00ff), .col23(32'hff00ff),
    .col24(32'hff00ff00), .col25(32'hff00ff00), .col26(32'hff00ff00), .col27(32'hff00ff00),
    .col28(32'hff00ff00), .col29(32'hff00ff00), .col30(32'hff00ff00), .col31(32'hff00ff00));
  DotMatrix #(.matrixcols(4), .matrixrows(32)) dotmatrix_6 (
    .col0(square_32_2_bus_0_2), .col1(square_32_2_bus_0_3), .col2(square_32_2_bus_0_4),
    .col3(square_32_2_bus_0_5));
  DotMatrix #(.matrixcols(4), .matrixrows(32)) dotmatrix_7 (
    .col0(square_32_1_bus_0_2), .col1(square_32_1_bus_0_3), .col2(square_32_1_bus_0_4),
    .col3(square_32_1_bus_0_5));
  square_32 square_32_1 (
    .bus_0(32'h72707171), .bus_0_2(square_32_1_bus_0_2), .bus_0_3(square_32_1_bus_0_3),
    .bus_0_4(square_32_1_bus_0_4), .bus_0_5(square_32_1_bus_0_5));
  square_32 square_32_2 (
    .bus_0(32'h27270717), .bus_0_2(square_32_2_bus_0_2), .bus_0_3(square_32_2_bus_0_3),
    .bus_0_4(square_32_2_bus_0_4), .bus_0_5(square_32_2_bus_0_5));
  Comparator #(.width(16), .mode("unsigned")) comparator_3 (
    .a(address_bus), .b(16'h8002), .eq(comparator_3_eq));  // open: gt, lt
  DotMatrix #(.matrixcols(4), .matrixrows(32)) dotmatrix_8 (
    .col0(square_32_4_bus_0_2), .col1(square_32_4_bus_0_3), .col2(square_32_4_bus_0_4),
    .col3(square_32_4_bus_0_5));
  DotMatrix #(.matrixcols(4), .matrixrows(32)) dotmatrix_9 (
    .col0(square_32_3_bus_0_2), .col1(square_32_3_bus_0_3), .col2(square_32_3_bus_0_4),
    .col3(square_32_3_bus_0_5));
  square_32 square_32_3 (
    .bus_0(32'h27270717), .bus_0_2(square_32_3_bus_0_2), .bus_0_3(square_32_3_bus_0_3),
    .bus_0_4(square_32_3_bus_0_4), .bus_0_5(square_32_3_bus_0_5));
  square_32 square_32_4 (
    .bus_0(32'h72707171), .bus_0_2(square_32_4_bus_0_2), .bus_0_3(square_32_4_bus_0_3),
    .bus_0_4(square_32_4_bus_0_4), .bus_0_5(square_32_4_bus_0_5));
  Button button_1 (.out(button_1_out));
  assign bit_extender_1_out = {{15{1'b0}}, button_1_out};  // Bit_Extender bit_extender_1
  and and_3 (dev_read, mem, comparator_3_eq, read);
  DotMatrix #(.matrixcols(4), .matrixrows(32)) dotmatrix_10 (
    .col0(square_32_5_bus_0_2), .col1(square_32_5_bus_0_3), .col2(square_32_5_bus_0_4),
    .col3(square_32_5_bus_0_5));
  DotMatrix #(.matrixcols(4), .matrixrows(32)) dotmatrix_11 (
    .col0(square_32_6_bus_0_2), .col1(square_32_6_bus_0_3), .col2(square_32_6_bus_0_4),
    .col3(square_32_6_bus_0_5));
  square_32 square_32_5 (
    .bus_0(32'h72707171), .bus_0_2(square_32_5_bus_0_2), .bus_0_3(square_32_5_bus_0_3),
    .bus_0_4(square_32_5_bus_0_4), .bus_0_5(square_32_5_bus_0_5));
  square_32 square_32_6 (
    .bus_0(32'h27270717), .bus_0_2(square_32_6_bus_0_2), .bus_0_3(square_32_6_bus_0_3),
    .bus_0_4(square_32_6_bus_0_4), .bus_0_5(square_32_6_bus_0_5));
  assign data_bus = dev_read ? bit_extender_1_out : 16'bz;  // Controlled_Buffer controlled_buffer_3
  Register #(.width(16)) register_1 (.D(data_bus), .en(dev_write), .Q(register_1_q), .clk(clock));  // open: clr
  DotMatrix #(.matrixcols(4), .matrixrows(32)) dotmatrix_12 (
    .col0(square_32_8_bus_0_2), .col1(square_32_8_bus_0_3), .col2(square_32_8_bus_0_4),
    .col3(square_32_8_bus_0_5));
  DotMatrix #(.matrixcols(4), .matrixrows(32)) dotmatrix_13 (
    .col0(square_32_7_bus_0_2), .col1(square_32_7_bus_0_3), .col2(square_32_7_bus_0_4),
    .col3(square_32_7_bus_0_5));
  square_32 square_32_7 (
    .bus_0(32'h27270717), .bus_0_2(square_32_7_bus_0_2), .bus_0_3(square_32_7_bus_0_3),
    .bus_0_4(square_32_7_bus_0_4), .bus_0_5(square_32_7_bus_0_5));
  square_32 square_32_8 (
    .bus_0(32'h72707171), .bus_0_2(square_32_8_bus_0_2), .bus_0_3(square_32_8_bus_0_3),
    .bus_0_4(square_32_8_bus_0_4), .bus_0_5(square_32_8_bus_0_5));
  DotMatrix #(.matrixcols(1), .matrixrows(16)) dotmatrix_14 (.col0(register_1_q));
  DotMatrix #(.matrixcols(27), .matrixrows(18)) dotmatrix_15 (
    .col0({12'h3f, undriven}), .col1({12'h3f, undriven}), .col2({12'h3f, undriven}),
    .col3({12'h3f, undriven}), .col4({12'h3f, undriven}), .col5({12'h3f, undriven}),
    .col6({12'h3f, undriven}), .col7({12'h3f, undriven}), .col8({12'h3f, undriven}),
    .col9({12'h3f, undriven}), .col10({12'h3f, undriven}), .col11({12'h3f, undriven}),
    .col12({12'h3f, undriven}), .col13({12'h3f, undriven}), .col14({12'h3f, undriven}),
    .col15({12'h3f, undriven}), .col16({12'h3f, undriven}), .col17({12'h3f, undriven}),
    .col18({12'h3f, undriven}), .col19({12'h3f, undriven}), .col20({12'h3f, undriven}),
    .col21({12'h3f, undriven}), .col22({12'h3f, undriven}), .col23({12'h3f, undriven}),
    .col24({12'h3f, undriven}), .col25({12'h3f, undriven}), .col26({12'h3f, undriven}));
endmodule

module square (
  input  [3:0] number0_4,
  output [3:0] bus_0,
  output [3:0] bus_1,
  output [3:0] bus_2,
  output [3:0] bus_3
);

  wire [1:1] type_2;
  wire [2:0] bit_extender_1_out;
  wire [2:1] type_1;

  Bit_Extender #(.in_width(4), .out_width(3)) bit_extender_1 (.in(number0_4), .out(bit_extender_1_out));
  Multiplexer #(.select(3), .width(4)) multiplexer_1 (
    .in0(4'b0000), .in1(4'b0110), .in2({1'b0, type_1, 1'b0}), .in3(4'b0110), .in4({1'b0, type_1, 1'b0}),
    .in5(4'b1111), .in6(4'b1111), .in7(4'b1111), .out(bus_1), .sel(bit_extender_1_out));  // open: en
  // Probe on bus_1
  Multiplexer #(.select(3), .width(4)) multiplexer_2 (
    .in0(4'b0000), .in1(4'b0110), .in2({1'b0, type_1, 1'b0}), .in3(4'b0010), .in4({2'b00, type_2[1], 1'b0}),
    .in5(4'b1111), .in6(4'b1111), .in7(4'b1111), .out(bus_2), .sel(bit_extender_1_out));  // open: en
  Multiplexer #(.select(3), .width(4)) multiplexer_3 (
    .in0(4'b0000), .in1(4'b0000), .in2(4'b0000), .in3(4'b0000), .in4(4'b0000), .in5(4'b1111), .in6(4'b1111),
    .in7(4'b1111), .out(bus_0), .sel(bit_extender_1_out));  // open: en

  assign bus_3 = bus_0;

  // Notes on the sheet:
  //   0 - пустая клетка
  //   1 - белая шашка
  //   2 - черная шашка
  //   3 - белая дамка
  //   4 - черная дамка
endmodule

module square_32 (
  input  [31:0] bus_0,
  output [31:0] bus_0_2,
  output [31:0] bus_0_3,
  output [31:0] bus_0_4,
  output [31:0] bus_0_5
);

  square square_1 (
    .number0_4(bus_0[3:0]), .bus_0(bus_0_2[3:0]), .bus_1(bus_0_3[3:0]), .bus_2(bus_0_4[3:0]),
    .bus_3(bus_0_5[3:0]));
  square square_2 (
    .number0_4(bus_0[7:4]), .bus_0(bus_0_2[7:4]), .bus_1(bus_0_3[7:4]), .bus_2(bus_0_4[7:4]),
    .bus_3(bus_0_5[7:4]));
  square square_3 (
    .number0_4(bus_0[11:8]), .bus_0(bus_0_2[11:8]), .bus_1(bus_0_3[11:8]), .bus_2(bus_0_4[11:8]),
    .bus_3(bus_0_5[11:8]));
  square square_4 (
    .number0_4(bus_0[15:12]), .bus_0(bus_0_2[15:12]), .bus_1(bus_0_3[15:12]), .bus_2(bus_0_4[15:12]),
    .bus_3(bus_0_5[15:12]));
  square square_5 (
    .number0_4(bus_0[19:16]), .bus_0(bus_0_2[19:16]), .bus_1(bus_0_3[19:16]), .bus_2(bus_0_4[19:16]),
    .bus_3(bus_0_5[19:16]));
  square square_6 (
    .number0_4(bus_0[23:20]), .bus_0(bus_0_2[23:20]), .bus_1(bus_0_3[23:20]), .bus_2(bus_0_4[23:20]),
    .bus_3(bus_0_5[23:20]));
  square square_7 (
    .number0_4(bus_0[27:24]), .bus_0(bus_0_2[27:24]), .bus_1(bus_0_3[27:24]), .bus_2(bus_0_4[27:24]),
    .bus_3(bus_0_5[27:24]));
  square square_8 (
    .number0_4(bus_0[31:28]), .bus_0(bus_0_2[31:28]), .bus_1(bus_0_3[31:28]), .bus_2(bus_0_4[31:28]),
    .bus_3(bus_0_5[31:28]));
endmodule
